# Fritzing sketch photoresistor (saved by Fritzing 0.8.7b)
breadboards: 1

parts:
  R5 = Photocell (LDR) [package=THT]
  元件1 = SunFounder Uno R3
  R4 = Resistor [tolerance=±5% resistance=220 package=THT]
  R6 = Resistor [tolerance=±5% resistance=220 package=THT]
  R7 = Resistor [tolerance=±5% resistance=220 package=THT]
  R8 = Resistor [tolerance=±5% resistance=220 package=THT]
  R9 = Resistor [tolerance=±5% resistance=220 package=THT]
  R10 = Resistor [tolerance=±5% resistance=220 package=THT]
  R11 = Resistor [tolerance=±5% resistance=220 package=THT]
  R12 = Resistor [tolerance=±5% resistance=220 package=THT]
  LED1 = LED - 5mm [color="Red (633nm)" package="5 mm [THT]"]
  LED2 = LED - 5mm [color="Red (633nm)" package="5 mm [THT]"]
  LED3 = LED - 5mm [color="Yellow (595nm)" package="5 mm [THT]"]
  LED4 = LED - 5mm [color="Yellow (592nm)" package="5 mm [THT]"]
  LED5 = LED - 5mm [color="Green (565nm)" package="5 mm [THT]"]
  LED6 = LED - 5mm [color="Green (565nm)" package="5 mm [THT]"]
  LED7 = LED - 5mm [color="Red (633nm)" package="5 mm [THT]"]
  LED8 = LED - 5mm [color="Red (633nm)" package="5 mm [THT]"]
  R13 = Resistor [tolerance=±5% resistance=10k package=THT]

nets:
  N1: R5.pin_0, 元件1.5V
  N2: R5.pin_1, 元件1.A0, R13.Pin_0
  N3: 元件1.D8, R7.Pin_0
  N4: 元件1.D9_PWM, R6.Pin_0
  N5: 元件1.D10_PWM/SS, R4.Pin_0
  N6: 元件1.D11_PWM/MOSI, R11.Pin_0
  N7: 元件1.D12/MISO, R9.Pin_0
  N8: 元件1.GND, LED1.cathode, LED2.cathode, LED3.cathode, LED4.cathode, LED5.cathode, LED6.cathode, LED7.cathode, LED8.cathode, R13.Pin_1
  N9: 元件1.D5_PWM, R12.Pin_0
  N10: 元件1.D6_PWM, R10.Pin_0
  N11: 元件1.D7, R8.Pin_0
  N12: R4.Pin_1, LED3.anode
  N13: R6.Pin_1, LED4.anode
  N14: R7.Pin_1, LED5.anode
  N15: R8.Pin_1, LED6.anode
  N16: R9.Pin_1, LED1.anode
  N17: R10.Pin_1, LED7.anode
  N18: R11.Pin_1, LED2.anode
  N19: R12.Pin_1, LED8.anode

custom parts:
  SunFounder Uno R3: The SunFounder Uno is a microcontroller board based on the ATmega328 (datasheet). It has 14 digital input/output pins (of which 6 can be used as PWM outputs), 6 analog inputs, a 16 MHz ceramic resonator, a USB connection, a power jack, an ICSP header, and a reset button. It contains everything needed to support the microcontroller; simply connect it to a computer with a USB cable or power it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
