# Fritzing sketch Thermistor (saved by Fritzing 0.8.7b)
breadboards: 1

parts:
  R5 = Resistor [tolerance=±5% resistance=10k package=THT]
  C1 = Ceramic Capacitor [capacitance=100nF package="100 mil [THT, multilayer]"]
  元件1 = SunFounder Uno R3

nets:
  N1: R5.Pin_0, C1.1, 元件1.A0
  N2: R5.Pin_1, 元件1.GND
  N3: C1.0, 元件1.5V

custom parts:
  SunFounder Uno R3: The SunFounder Uno is a microcontroller board based on the ATmega328 (datasheet). It has 14 digital input/output pins (of which 6 can be used as PWM outputs), 6 analog inputs, a 16 MHz ceramic resonator, a USB connection, a power jack, an ICSP header, and a reset button. It contains everything needed to support the microcontroller; simply connect it to a computer with a USB cable or power it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
